# Fritzing sketch kairo (saved by Fritzing 0.9.3b)
breadboards: 1

parts:
  LED2 = LED - 5mm [color="Red (633nm)" package="5 mm [THT]"]
  S1 = Pushbutton [package="[THT]"]
  LED1 = LED - 5mm [color="Red (633nm)" package="5 mm [THT]"]
  Raspberry_Pi_ＧＰＩＯ1 = AE-RBPI-BOB40KIT
  MIC1 = Microphone

nets (from the breadboard view):
  N1: LED2.cathode, Raspberry_Pi_ＧＰＩＯ1.GPIO26
  N2: LED2.anode, LED1.anode, Raspberry_Pi_ＧＰＩＯ1.GND, MIC1.pin1
  N3: S1.Pin_1, S1.Pin_2
  N4: S1.Pin_3, S1.Pin_4, Raspberry_Pi_ＧＰＩＯ1.GPIO6
  N5: Raspberry_Pi_ＧＰＩＯ1.GPIO13, MIC1.pin2

custom parts:
  AE-RBPI-BOB40KIT: http://akizukidenshi.com/catalog/g/gK-08892/
